# Fritzing sketch Can (saved by Fritzing 0.9.4)
breadboards: 1

parts:
  Mod2 = Raspberry Pi Pico W  # not connected
  LED16 = smd LED [color="Red (633nm)" package="1206 [SMD]"]
  BT6 = Bluetooth HC-06u [package=THT]
  LED17 = smd LED [color="Red (633nm)" package="1206 [SMD]"]
  LED18 = smd LED [color="Red (633nm)" package="1206 [SMD]"]
  R16 = Resistor [tolerance=±5% resistance=220 package="2512 [SMD]"]
  R17 = Resistor [tolerance=±5% resistance=220 package="2512 [SMD]"]
  R18 = Resistor [tolerance=±5% resistance=220 package="2512 [SMD]"]
  Sensor2 = TTP223B Capacitive Touch Sensor Module
  J2 = Basic Servo

nets:
  GND: LED16.cathode, BT6.GND, LED17.cathode, LED18.cathode, Sensor2.GND
  N1: LED16.anode, R18.Pin_1
  VCC: BT6.VCC, Sensor2.VCC, J2.vcc
  N2: LED17.anode, R16.Pin_1
  N3: LED18.anode, R17.Pin_1

custom parts:
  Raspberry Pi Pico W: Raspberry Pi Pico W. Based around the RP2040 microcontroller the Pico W is a low cost microcontroller device bringing Raspberry Pi quality, cost, and easy of use to the microcontroller space. The areas marked KEEPOUT in pcb silkscreen should not have traces running through them to avoid shorts on a soldered in module!
  Bluetooth HC-06u: Bluetooth HC-06 - face up, pins down 16.5mm x 37.5mm PCB
  TTP223B Capacitive Touch Sensor Module: The TTP223B capacitive touch sensor module uses the TTP223B IC. The appropriate voltage is approximately 2 to 5.5 volts.
